# Fritzing sketch ESP8266_lamp (saved by Fritzing 0.9.2b)

parts:
  Part1 = SparkFun ESP8266 Thing
  LED2 = Super Flux RGB LED (com. cathode)
  R1 = Resistor [tolerance=±5% resistance=220 package="2010 [SMD]"]
  R2 = Resistor [tolerance=±5% resistance=220 package="2010 [SMD]"]
  R4 = Resistor [tolerance=±5% resistance=33k package="2010 [SMD]"]
  R3 = Resistor [tolerance=±5% resistance=220 package="2010 [SMD]"]
  R6 = Slide Potentiometer [maximum_resistance=100kΩ]

nets:
  N1: Part1.VCC, R4.Pin_0
  N2: Part1.GND, R6.leg1
  N3: Part1.GPIO4, R2.Pin_1
  N4: Part1.GPIO13, R1.Pin_1
  N5: Part1.GPIO12, R3.Pin_0
  N6: Part1.ADC, R6.wiper
  N7: LED2.red_anode, R3.Pin_1
  N8: LED2.blue_anode, R2.Pin_0
  N9: LED2.green_anode, R1.Pin_0
  N10: R4.Pin_1, R6.leg2

notes:
  Resistor value is at least 2.3*the potentiometer resistance. For example, a 10k potentiometer needs a 23k resistor.
  Resistor values
  depend on the LED.
